# Fritzing sketch ferdoVision (saved by Fritzing 0.8.0b)
breadboards: 2

parts:
  BeagleBone1 = BeagleBone Black
  C1 = Electrolytic Capacitor [capacitance=47µF voltage=20V package="100 mil [THT, electrolytic]"]
  C2 = Electrolytic Capacitor [capacitance=1µF package="100 mil [THT, electrolytic]"]
  R1 = Resistor [tolerance=±5% resistance=10k package=THT]
  R2 = Resistor [tolerance=±5% resistance=220 package=THT]
  CAMERA1 = TTL Serial JPEG Camera

nets:
  N1: BeagleBone1.no_name_yet#1, C1.-, C2.-, R1.Pin_1, CAMERA1.GND
  N2: BeagleBone1.no_name_yet#5, C1.+, C2.+, CAMERA1.5V
  N3: BeagleBone1.no_name_yet#24, R2.Pin_1
  N4: BeagleBone1.no_name_yet#26, CAMERA1.TX
  N5: R1.Pin_0, R2.Pin_0, CAMERA1.RX

custom parts:
  BeagleBone Black: BeagleBone Black rev. A5B
  TTL Serial JPEG Camera: TTL Serial JPEG Camera with NTSC Out
